# Fritzing sketch button1 (saved by Fritzing 0.9.4)
breadboards: 1

parts:
  Raspberry_Pi_1 = Raspberry Pi 3 [part_number=RPI-3-V1.2]
  R1 = Resistor [tolerance=±5% resistance=220 package=THT]
  LED1 = LED - 5mm [color="Red (633nm)" package="5 mm [THT]"]
  S1 = Pushbutton [package="[THT]"]

nets:
  N1: Raspberry_Pi_1.3v3, S1.Pin_3, S1.Pin_4
  N2: Raspberry_Pi_1.GPIO4, LED1.anode
  N3: Raspberry_Pi_1.GPIO14, S1.Pin_1, S1.Pin_2
  N4: Raspberry_Pi_1.GND, R1.Pin_0
  N5: R1.Pin_1, LED1.cathode
